// Logisim project Address Decode.circ as structural Verilog: 2 circuits, main circuit Scratchpad
module Scratchpad (
  input  VPB,
  input  in_2,
  input  in_3,
  input  in_4,
  input  in_5,
  input  in_6,
  input  in_7,
  input  in_8,
  input  in_9,
  input  in_10,
  input  in_11,
  input  in_12,
  input  in_13,
  input  in_14,
  input  in_15,
  input  in_16,
  input  in_17,
  input  in_18,
  input  in_19,
  input  in_20,
  input  in_21,
  input  in_22,
  input  in_23,
  input  in_24,
  input  in_25
);

  wire and_1_out, and_2_out, and_3_out, and_4_out, comparator_1_gt, comparator_2_eq, counter_1_carry,
       d_ff_1_q, INT, IRQ, NMI, not_2_out, not_3_out, not_4_out, not_5_out, or_1_out, or_2_out, or_3_out,
       PHI2, pull_resistor_1_node, pull_resistor_2_node, pull_resistor_3_node, pull_resistor_5_node,
       pull_resistor_8_node, pull_resistor_9_node, pull_resistor_11_node, pull_resistor_15_node,
       pull_resistor_16_node, R_WB_out, undriven, undriven_2, undriven_3, undriven_4, undriven_5, undriven_6,
       VPB_t;
  wire [2:0] priority_encoder_1_out, priority_encoder_3_out;
  wire [3:0] controlled_buffer_2_out, controlled_buffer_4_out, counter_2_q, pull_resistor_7_node;
  wire [3:3] pull_resistor_4_node, pull_resistor_6_node;
  wire [7:0] Address_out, controlled_buffer_1_out, pull_resistor_10_node, register_1_q;
  wire [15:0] Address_2_out, multiplexer_1_out;
  wire [15:15] pull_resistor_12_node;

  Pull_Resistor #(.pull(1)) pull_resistor_1 (.node(pull_resistor_1_node));
  Counter #(.width(2), .max('h3)) counter_1 (.carry(counter_1_carry), .clk(PHI2));  // open: load, D, count, Q, clr
  Clock clock_1 (.out(PHI2));
  LED u_NMI (.in(NMI));
  LED u_IRQ (.in(IRQ));
  Pull_Resistor #(.pull(1)) pull_resistor_2 (.node(pull_resistor_2_node));
  Pull_Resistor #(.pull(1)) pull_resistor_3 (.node(pull_resistor_3_node));
  Random Address (.clk(counter_1_carry), .next(pull_resistor_1_node), .out(Address_out));  // open: clr
  Counter #(.width(4), .max('hf)) counter_2 (
    .D(4'b0000), .Q(counter_2_q), .clk(PHI2), .clr(or_1_out));  // open: load, count, carry
  or or_1 (or_1_out, INT, comparator_2_eq);
  or or_2 (or_2_out, VPB, comparator_1_gt);
  not not_1 (VPB_t, or_2_out);
  Register #(.trigger("high")) Bank_Address (.D({8{1'b0}}), .clk(counter_1_carry));  // open: en, Q, clr
  Random #(.width(16)) Address_2 (
    .clk(counter_1_carry), .next(pull_resistor_2_node), .out(Address_2_out));  // open: clr
  Random #(.width(1)) R_WB (.clk(counter_1_carry), .next(pull_resistor_3_node), .out(R_WB_out));  // open: clr
  not not_2 (not_2_out, R_WB_out);
  // Probe on controlled_buffer_1_out
  // Probe on Address_out
  Comparator #(.width(4), .mode("unsigned")) comparator_1 (
    .a(counter_2_q), .b(4'b0101), .gt(comparator_1_gt));  // open: eq, lt
  Comparator #(.width(4), .mode("unsigned")) comparator_2 (
    .a(counter_2_q), .b(4'b1000), .eq(comparator_2_eq));  // open: gt, lt
  or or_3 (or_3_out, not_2_out, INT);
  not not_3 (not_3_out, or_3_out);
  assign controlled_buffer_1_out = not_3_out ? Address_out : 8'bz;  // Controlled_Buffer controlled_buffer_1
  Pull_Resistor pull_resistor_4 (.node(pull_resistor_4_node[3]));
  // Probe on priority_encoder_1_out
  Priority_Encoder #(.disabled(0)) priority_encoder_1 (
    .in0(in_2), .in1(in_3), .in2(in_4), .in3(in_5), .in4(in_6), .in5(in_7), .in6(in_8), .in7(in_9),
    .out(priority_encoder_1_out), .en_in(pull_resistor_5_node));
  assign controlled_buffer_2_out = and_1_out ? {pull_resistor_4_node[3], priority_encoder_1_out} : 4'bz;  // Controlled_Buffer controlled_buffer_2
  and and_1 (and_1_out, undriven, not_4_out);
  not not_4 (not_4_out, undriven_2);
  Pull_Resistor #(.pull(1)) pull_resistor_5 (.node(pull_resistor_5_node));
  not Interrupt (INT, and_2_out);
  and and_2 (and_2_out, undriven_3, undriven_6, undriven_4);
  Pull_Resistor pull_resistor_6 (.node(pull_resistor_6_node[3]));
  assign controlled_buffer_2_out = and_3_out ? pull_resistor_7_node : 4'bz;  // Controlled_Buffer controlled_buffer_3
  Pull_Resistor #(.pull(1)) pull_resistor_7 (.node(pull_resistor_7_node[3]));
  Priority_Encoder #(.disabled(0)) priority_encoder_2 (
    .in0(in_10), .in1(in_11), .in2(in_12), .in3(in_13), .in4(in_14), .in5(in_15), .in6(in_16), .in7(in_17),
    .out(pull_resistor_7_node[2:0]), .en_in(pull_resistor_8_node));
  assign controlled_buffer_4_out = and_3_out ? {4{pull_resistor_6_node[3]}} : 4'bz;  // Controlled_Buffer controlled_buffer_4
  // Probe on pull_resistor_7_node[2:0]
  or or_4 (IRQ, undriven, undriven_5);
  Pull_Resistor #(.pull(1)) pull_resistor_8 (.node(pull_resistor_8_node));
  // Probe on {controlled_buffer_4_out[3:1], controlled_buffer_2_out, controlled_buffer_4_out[0]}
  D_Flip_Flop #(.trigger("high")) d_ff_1 (
    .clk(PHI2), .D(IRQ), .Q(d_ff_1_q), .en(pull_resistor_9_node));  // open: Qn, preset, reset
  Pull_Resistor #(.pull(1)) pull_resistor_9 (.node(pull_resistor_9_node));
  and and_3 (and_3_out, undriven_5, not_5_out);
  Register #(.trigger("high")) register_1 (
    .D({controlled_buffer_4_out[3:1], controlled_buffer_2_out, controlled_buffer_4_out[0]}),
    .Q(register_1_q), .clk(and_4_out));  // open: en, clr
  and and_4 (and_4_out, VPB_t, d_ff_1_q);
  assign {controlled_buffer_4_out[3:1], controlled_buffer_2_out, controlled_buffer_4_out[0]} = NMI ? {{2{pull_resistor_10_node[7]}}, pull_resistor_10_node[5], pull_resistor_10_node[7], priority_encoder_3_out, pull_resistor_10_node[0]} : 8'bz;  // Controlled_Buffer controlled_buffer_5
  not not_5 (not_5_out, NMI);
  // Probe on {{2{pull_resistor_10_node[7]}}, pull_resistor_10_node[5], pull_resistor_10_node[7], priority_encoder_3_out, pull_resistor_10_node[0]}
  Pull_Resistor pull_resistor_10 (.node(pull_resistor_10_node[0]));
  // Probe on priority_encoder_3_out
  Priority_Encoder #(.disabled(0)) priority_encoder_3 (
    .in0(in_18), .in1(in_19), .in2(in_20), .in3(in_21), .in4(in_22), .in5(in_23), .in6(in_24), .in7(in_25),
    .out(priority_encoder_3_out), .en_in(pull_resistor_11_node));
  Pull_Resistor #(.pull(1)) pull_resistor_11 (.node(pull_resistor_11_node));
  Pull_Resistor #(.pull(1)) pull_resistor_12 (.node(pull_resistor_12_node[15]));
  Pull_Resistor #(.pull(1)) pull_resistor_13 (.node(pull_resistor_10_node[5]));
  Pull_Resistor pull_resistor_14 (.node(pull_resistor_10_node[7]));
  // Probe on Address_2_out
  Pull_Resistor #(.pull(1)) pull_resistor_15 (.node(pull_resistor_15_node));
  // Probe on {{8{pull_resistor_12_node[15]}}, register_1_q}
  // Probe on multiplexer_1_out
  Multiplexer #(.width(16)) multiplexer_1 (
    .in0(Address_2_out), .in1({{8{pull_resistor_12_node[15]}}, register_1_q}), .out(multiplexer_1_out),
    .sel(INT), .en(pull_resistor_15_node));
  Pull_Resistor #(.pull(1)) pull_resistor_16 (.node(pull_resistor_16_node));
  RAM #(.addrWidth(16)) ram_1 (
    .addr(multiplexer_1_out), .data(controlled_buffer_1_out), .sel(pull_resistor_16_node), .clk(PHI2),
    .ld(or_3_out));  // open: clr
endmodule

module Interrupt_decode (
  input  INT0,
  input  in_2,
  input  in_3,
  input  in_4,
  input  in_5,
  input  in_6,
  input  in_7,
  input  in_8,
  input  in_9,
  input  in_10,
  input  in_11,
  input  in_12,
  input  in_13,
  input  in_14,
  input  in_15,
  input  in_16
);

  wire ADDR_0, and_1_out, and_2_out, not_1_out, or_1_out, pull_resistor_2_node, pull_resistor_4_node,
       undriven, undriven_2, VPB;
  wire [3:0] pull_resistor_1_node, pull_resistor_3_node;
  wire [7:1] controlled_buffer_1_out;
  wire [15:0] INT_ADDR;

  Pull_Resistor pull_resistor_1 (.node(pull_resistor_1_node[3]));
  // Probe on pull_resistor_1_node[2:0]
  Priority_Encoder #(.disabled(0)) priority_encoder_1 (
    .in0(INT0), .in1(in_2), .in2(in_3), .in3(in_4), .in4(in_5), .in5(in_6), .in6(in_7), .in7(in_8),
    .out(pull_resistor_1_node[2:0]), .en_in(pull_resistor_2_node));
  assign controlled_buffer_1_out[4:1] = and_1_out ? pull_resistor_1_node : 4'bz;  // Controlled_Buffer controlled_buffer_1
  and and_1 (and_1_out, undriven_2, not_1_out);
  not not_1 (not_1_out, undriven);
  Pull_Resistor #(.pull(1)) pull_resistor_2 (.node(pull_resistor_2_node));
  Pull_Resistor #(.pull(1)) pull_resistor_3 (.node(pull_resistor_3_node[3]));
  // Probe on pull_resistor_3_node[2:0]
  Priority_Encoder #(.disabled(0)) priority_encoder_2 (
    .in0(in_9), .in1(in_10), .in2(in_11), .in3(in_12), .in4(in_13), .in5(in_14), .in6(in_15), .in7(in_16),
    .out(pull_resistor_3_node[2:0]), .en_in(pull_resistor_4_node));
  assign controlled_buffer_1_out[4:1] = undriven ? pull_resistor_3_node : 4'bz;  // Controlled_Buffer controlled_buffer_2
  Pull_Resistor #(.pull(1)) pull_resistor_4 (.node(pull_resistor_4_node));
  Pull_Resistor pull_resistor_5 (.node(controlled_buffer_1_out[7]));
  // Probe on {{3{controlled_buffer_1_out[7]}}, controlled_buffer_1_out[4:1], ADDR_0}
  Register #(.trigger("high")) register_1 (
    .D({{3{controlled_buffer_1_out[7]}}, controlled_buffer_1_out[4:1], ADDR_0}), .Q(INT_ADDR[7:0]),
    .clk(and_2_out));  // open: en, clr
  and and_2 (and_2_out, VPB, or_1_out);
  or or_1 (or_1_out, undriven_2, undriven);
  Pull_Resistor #(.pull(1)) pull_resistor_6 (.node(INT_ADDR[15]));
  // Probe on {{8{INT_ADDR[15]}}, INT_ADDR[7:0]}

  // Other names for the same wires on the sheet: INT_ADDR[14:8] = {7{INT_ADDR[15]}}
endmodule
