// Logisim project Memory_Copier.circ as structural Verilog: 1 circuit, main circuit main
module main (
);

  wire CLK, clock_1_out, clock_2_out, CNT, d_ff_1_q, d_ff_1_qn, d_ff_2_q, ds1813_1_p2, LE, lvc161_1_p8,
       lvc161_2_p8, lvc161_3_p8, lvc161_4_p8, lvc161_6_p8, lvc161_7_p8, not_1_out, PEB, pull_resistor_2_node,
       pull_resistor_3_node, pull_resistor_4_node, pull_resistor_5_node, pull_resistor_6_node,
       pull_resistor_7_node, pull_resistor_8_node, pull_resistor_9_node, pull_resistor_10_node,
       pull_resistor_11_node, pull_resistor_13_node, pull_resistor_14_node, pull_resistor_15_node,
       pull_resistor_16_node, pull_resistor_17_node, pull_resistor_18_node, READ, WRITE;
  wire [2:2] pull_resistor_12_node;
  wire [3:0] lvc161_1_p7, lvc161_2_p7, lvc161_3_p7, lvc161_4_p7, lvc161_5_p6, lvc161_6_p7, lvc161_7_p7,
       lvc161_8_p7, lvc161_9_p7;
  wire [7:0] lvc138_1_p5, ram_1_data;
  wire [23:0] DESTINATION_ADDRESS, SOURCE_ADDRESS;

  Clock clock_1 (.out(clock_1_out));
  Pull_Resistor #(.pull(1)) pull_resistor_1 (.node(CNT));
  // DS1813 ds1813_1: pin names not known; wires that end beside it: clock_1_out, ds1813_1_p2, ds1813_1_p2
  Clock clock_2 (.out(clock_2_out));
  not not_1 (not_1_out, clock_2_out);
  Pull_Resistor #(.pull(1)) pull_resistor_2 (.node(pull_resistor_2_node));
  Pull_Resistor #(.pull(1)) pull_resistor_3 (.node(pull_resistor_3_node));
  Pull_Resistor #(.pull(1)) pull_resistor_4 (.node(pull_resistor_4_node));
  Pull_Resistor #(.pull(1)) pull_resistor_5 (.node(pull_resistor_5_node));
  D_Flip_Flop d_ff_1 (.clk(clock_2_out), .D(ds1813_1_p2), .Q(d_ff_1_q), .Qn(d_ff_1_qn));  // open: preset, reset
  D_Flip_Flop d_ff_2 (.clk(not_1_out), .D(d_ff_1_qn), .Q(d_ff_2_q));  // open: Qn, preset, reset
  // LVC161 lvc161_1: pin names not known; wires that end beside it: pull_resistor_2_node, PEB, 4'b0111, CLK, pull_resistor_3_node, CNT, lvc161_1_p7, lvc161_1_p8
  // LVC161 lvc161_2: pin names not known; wires that end beside it: pull_resistor_4_node, PEB, 4'b0000, CLK, pull_resistor_5_node, CNT, lvc161_2_p7, lvc161_2_p8
  and and_1 (LE, d_ff_1_q, d_ff_2_q);
  not not_2 (PEB, LE);
  Pull_Resistor #(.pull(1)) pull_resistor_6 (.node(pull_resistor_6_node));
  Pull_Resistor #(.pull(1)) pull_resistor_7 (.node(pull_resistor_7_node));
  Pull_Resistor #(.pull(1)) pull_resistor_8 (.node(pull_resistor_8_node));
  // LVC161 lvc161_3: pin names not known; wires that end beside it: pull_resistor_7_node, PEB, 4'b1010, CLK, lvc161_1_p8, CNT, lvc161_3_p7, lvc161_3_p8
  // LVC161 lvc161_4: pin names not known; wires that end beside it: pull_resistor_8_node, PEB, 4'b0000, CLK, lvc161_2_p8, CNT, lvc161_4_p7, lvc161_4_p8
  // LVC161 lvc161_5: pin names not known; wires that end beside it: ds1813_1_p2, pull_resistor_6_node, clock_2_out, pull_resistor_6_node, CNT, lvc161_5_p6
  Pull_Resistor #(.pull(1)) pull_resistor_9 (.node(pull_resistor_9_node));
  Pull_Resistor #(.pull(1)) pull_resistor_10 (.node(pull_resistor_10_node));
  // LVC161 lvc161_6: pin names not known; wires that end beside it: pull_resistor_9_node, PEB, 4'b0011, CLK, lvc161_3_p8, CNT, lvc161_6_p7, lvc161_6_p8
  // LVC161 lvc161_7: pin names not known; wires that end beside it: pull_resistor_10_node, PEB, 4'b0000, CLK, lvc161_4_p8, CNT, lvc161_7_p7, lvc161_7_p8
  Pull_Resistor pull_resistor_11 (.node(pull_resistor_11_node));
  Pull_Resistor pull_resistor_12 (.node(pull_resistor_12_node[2]));
  Pull_Resistor #(.pull(1)) pull_resistor_13 (.node(pull_resistor_13_node));
  RAM #(.addrWidth(24), .databus("bidir"), .enables("line"), .trigger("high"), .\type ("nonvolatile")) ram_1 (
    .addr(SOURCE_ADDRESS), .data(ram_1_data));  // open: we, oe, clk
  // NOT_Gate not_3 has open pins: in=READ, out=open
  // NOT_Gate not_4 has open pins: in=WRITE, out=open
  // NOT_Gate not_5 has open pins: in=pull_resistor_14_node, out=open
  Pull_Resistor pull_resistor_14 (.node(pull_resistor_14_node));
  // LVC138 lvc138_1: pin names not known; wires that end beside it: pull_resistor_11_node, pull_resistor_11_node, {pull_resistor_12_node[2], lvc161_5_p6[1:0]}, pull_resistor_13_node, lvc138_1_p5
  Pull_Resistor #(.pull(1)) pull_resistor_15 (.node(pull_resistor_15_node));
  Pull_Resistor #(.pull(1)) pull_resistor_16 (.node(pull_resistor_16_node));
  // LVC161 lvc161_8: pin names not known; wires that end beside it: pull_resistor_15_node, PEB, 4'b1111, CLK, lvc161_6_p8, CNT, lvc161_8_p7
  // LVC161 lvc161_9: pin names not known; wires that end beside it: pull_resistor_16_node, PEB, 4'b0110, CLK, lvc161_7_p8, CNT, lvc161_9_p7
  nand nand_1 (READ, lvc138_1_p5[0], lvc138_1_p5[1]);
  not not_6 (CLK, lvc138_1_p5[3]);
  not not_7 (WRITE, lvc138_1_p5[3]);
  // Probe on ram_1_data
  Pull_Resistor pull_resistor_17 (.node(pull_resistor_17_node));
  Pull_Resistor pull_resistor_18 (.node(pull_resistor_18_node));
  // LVC573 lvc573_1: pin names not known; wires that end beside it: READ, 8'h1, LE, SOURCE_ADDRESS[23:16]
  // LVC164245 lvc164245_1: pin names not known; wires that end beside it: READ, READ, {lvc161_8_p7, lvc161_6_p7}, pull_resistor_17_node, {lvc161_3_p7, lvc161_1_p7}, pull_resistor_17_node, SOURCE_ADDRESS[15:8], SOURCE_ADDRESS[7:0]
  // LVC573 lvc573_2: pin names not known; wires that end beside it: READ, {8{1'b0}}, LE, DESTINATION_ADDRESS[23:16]
  // LVC164245 lvc164245_2: pin names not known; wires that end beside it: READ, READ, {lvc161_9_p7, lvc161_7_p7}, pull_resistor_18_node, {lvc161_4_p7, lvc161_2_p7}, pull_resistor_18_node, DESTINATION_ADDRESS[15:8], DESTINATION_ADDRESS[7:0]
endmodule
