// Logisim project demo2.circ as structural Verilog: 1 circuit, main circuit main
module main (
);

  wire not_1_out, PHI2, w65c816s_1_p3, w65c816s_1_p4;
  wire [7:0] lvc4245_1_p4;
  wire [15:0] w65c816s_1_p2;

  Clock clock_1 (.out(PHI2));
  // W65C816S w65c816s_1: pin names not known; wires that end beside it: PHI2, w65c816s_1_p2, w65c816s_1_p3, w65c816s_1_p4
  not not_1 (not_1_out, PHI2);
  // LVC4245 lvc4245_1: pin names not known; wires that end beside it: not_1_out, w65c816s_1_p3, w65c816s_1_p4, lvc4245_1_p4
  RAM #(.addrWidth(16), .databus("bidir"), .trigger("high"), .\type ("nonvolatile")) ram_1 (
    .addr(w65c816s_1_p2), .we(w65c816s_1_p4), .data(lvc4245_1_p4));  // open: oe
endmodule
